# Fritzing sketch CeilingSpotlightSketch (saved by Fritzing 0.9.4)

parts:
  IR1 = TSOP312.., 314.. [part_number=TSOP31238 package=THT]
  reading_light_LEDs = LEDs [package=led10mm]
  Power_plug1 = Power plug [part_number=12V]
  Attiny85 = Digispark
  status_LED_(red) = LEDs [package=led10mm]
  Q3 = MOSFET-NCHANNEL [part_number="IRLZ 34N" package=to220v]
  Q4 = MOSFET-NCHANNEL [part_number="IRLZ 34N" package=to220v]
  ceiling_light_LEDs = LEDs [package=led10mm]

nets:
  GND: IR1.GND, Power_plug1.GND, Attiny85.GND, status_LED_(red).C, Q3.S, Q4.S
  N1: IR1.Vs, Attiny85.VCC
  N2: IR1.Data, Attiny85.P2
  N3: reading_light_LEDs.C, Q4.D
  VCC: reading_light_LEDs.A, Power_plug1.VCC, Attiny85.VIN, ceiling_light_LEDs.A
  N4: Attiny85.P0, Q3.G
  N5: Attiny85.P1, status_LED_(red).A
  N6: Attiny85.P4, Q4.G
  N7: Q3.D, ceiling_light_LEDs.C

custom parts:
  Digispark: The Digispark is an Attiny85 based microcontroller development board similar to the Arduino line, only cheaper, smaller, and a bit less powerful. With a whole host of shields to extend its functionality and the ability to use the familiar Arduino IDE the Digispark is a great way to jump into electronics, or perfect for when an Arduino is too big or too much.
